# Fritzing sketch toaster (saved by Fritzing 0.7.0b)
perfboards: 1

parts:
  Part1 = Bluetooth Mate Silver
  R5 = Resistor [tolerance=±5% resistance=5.1k package=THT]
  R4 = Resistor [tolerance=±5% resistance=2.2k package=THT]
  R3 = Resistor [tolerance=±5% resistance=1k package=THT]
  R2 = Resistor [tolerance=±5% resistance=0 package=THT]
  R1 = Resistor [tolerance=±5% resistance=10k package=THT]
  Set_Shade_Out = female pin header, 1 pin [form="♀ (female)"]
  R6 = Resistor [tolerance=±5% resistance=10k package=THT]
  R7 = Resistor [tolerance=±5% resistance=10k package=THT]
  R8 = Resistor [tolerance=±5% resistance=10k package=THT]
  R9 = Resistor [tolerance=±5% resistance=10k package=THT]
  R12 = Resistor [tolerance=±5% resistance=5.1k package=THT]
  R11 = Resistor [tolerance=±5% resistance=5.1k package=THT]
  R10 = Resistor [tolerance=±5% resistance=5.1k package=THT]
  Control_Out = female pin header, 1 pin [form="♀ (female)"]
  5v = female pin header, 1 pin [form="♀ (female)"]
  R13 = Resistor [tolerance=±5% resistance=2.2k package=THT]
  Toast_LED_In = female pin header, 1 pin [form="♀ (female)"]
  Larson_Scanner_Out = female pin header, 1 pin [form="♀ (female)"]
  Reset_Toaster_Out = female pin header, 1 pin [form="♀ (female)"]
  Buttons_In = female pin header, 1 pin [form="♀ (female)"]
  Shade_Pot_In = female pin header, 1 pin [form="♀ (female)"]
  Part3 = OSEPP™ Pro Mini 5V
  Gnd = female pin header, 1 pin [form="♀ (female)"]

nets:
  N1: Part1.RTS_5V, Part3.DTR
  N2: Part1.RX_5V, Part3.TXO
  N3: Part1.TX_5V, Part3.RXI
  N4: Part1.VCC, Part3.VCC#17
  N5: Part1.CTS_5V, Part3.GND#18
  N6: Part1.GND, Part3.GND#19
  N7: R5.Pin_0, Part3.D6
  N8: R5.Pin_1, R4.Pin_1, R3.Pin_1, R2.Pin_1, R1.Pin_1, Control_Out.pin1
  N9: R4.Pin_0, Part3.D7
  N10: R3.Pin_0, Part3.D8
  N11: R2.Pin_0, Part3.D9
  N12: R1.Pin_0, Part3.D10
  N13: Set_Shade_Out.pin1, R6.Pin_1, R10.Pin_1
  N14: R6.Pin_0, Part3.D5
  N15: R7.Pin_0, Part3.D4
  N16: R7.Pin_1, R11.Pin_1, R10.Pin_0
  N17: R8.Pin_0, Part3.D3
  N18: R8.Pin_1, R12.Pin_1, R11.Pin_0
  N19: R9.Pin_0, Part3.D2
  N20: R9.Pin_1, R12.Pin_0
  N21: 5v.pin1, Part3.VCC#25
  N22: R13.Pin_0, Toast_LED_In.pin1, Part3.D11/MOSI
  N23: R13.Pin_1, Part3.GND#23, Gnd.pin1
  N24: Larson_Scanner_Out.pin1, Part3.D12/MISO
  N25: Reset_Toaster_Out.pin1, Part3.D13/SCK
  N26: Buttons_In.pin1, Part3.A0
  N27: Shade_Pot_In.pin1, Part3.A1

notes:
  Project Centurion, Toaster modification to add Bluetooth control and Cylon effects., 1.0

custom parts:
  OSEPP™ Pro Mini 5V: Description: It's blue! It's thin (0.8mm)! It's the Arduino Pro Mini! SparkFun's minimal design approach to Arduino. This is a 3.3V Arduino running the 8MHz bootloader (select 'Arduino Duemilanove w/ 328' within the Arduino software). Arduino Pro Mini does not come with connectors populated so that you can solder in any connector or wire with any orientation you need. We recommend first time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
